// Logisim project rcd.circ as structural Verilog: 1 circuit, main circuit main
module main (
);

  wire and_5_out, and_6_out, and_7_out, and_14_out, and_15_out, and_16_out, and_25_out, and_28_out,
       and_29_out, clock_1_out, not_1_out, not_2_out, not_3_out, not_4_out, not_5_out, not_6_out, not_7_out,
       not_8_out, not_9_out, not_10_out, not_11_out, not_12_out, undriven_8, undriven_13;
  wire [1:0] undriven, undriven_5, undriven_10;
  wire [3:0] and_10_out, and_11_out, and_21_out, and_22_out, and_31_out, and_32_out, undriven_2, undriven_3,
       undriven_6, undriven_7, undriven_11, undriven_12;
  wire [7:0] controlled_buffer_1_out, controlled_buffer_4_out, controlled_buffer_5_out, counter_1_q,
       ram_1_data, ram_2_data, ram_3_data, undriven_4, undriven_9, undriven_14;

  Clock clock_1 (.out(clock_1_out));
  Counter counter_1 (.Q(counter_1_q), .clk(clock_1_out));  // open: load, D, count, carry, clr
  ROM #(.dataWidth(32)) rom_1 (.addr(counter_1_q));  // open: data, sel
  and and_1 (and_10_out[3], and_5_out, undriven_2[3]);
  and and_2 (and_11_out[3], and_5_out, undriven_3[3]);
  not not_1 (not_1_out, undriven[1]);
  not not_2 (not_2_out, undriven[0]);
  and and_3 (and_10_out[2], and_5_out, undriven_2[2]);
  and and_4 (and_11_out[2], and_5_out, undriven_3[2]);
  not not_3 (not_3_out, and_7_out);
  not not_4 (not_4_out, clock_1_out);
  and and_5 (and_5_out, undriven[0], undriven[1]);
  and and_6 (and_6_out, undriven[0], not_1_out);
  and and_7 (and_7_out, not_2_out, undriven[1]);
  and and_8 (and_10_out[1], and_5_out, undriven_2[1]);
  and and_9 (and_11_out[1], and_5_out, undriven_3[1]);
  assign controlled_buffer_1_out = and_6_out ? ram_1_data : 8'bz;  // Controlled_Buffer controlled_buffer_1
  RAM #(.addrWidth(4)) ram_1 (
    .addr(undriven_3), .data(ram_1_data), .sel(1'b1), .clk(not_4_out), .ld(not_3_out), .clr(1'b0));
  assign ram_1_data = and_7_out ? undriven_4 : 8'bz;  // Controlled_Buffer controlled_buffer_2
  and and_10 (and_10_out[0], and_5_out, undriven_2[0]);
  and and_11 (and_11_out[0], and_5_out, undriven_3[0]);
  and and_12 (and_21_out[3], and_14_out, undriven_6[3]);
  and and_13 (and_22_out[3], and_14_out, undriven_7[3]);
  not not_5 (not_5_out, undriven_8);
  not not_6 (not_6_out, and_16_out);
  and and_14 (and_14_out, undriven_5[0], undriven_5[1]);
  and and_15 (and_15_out, undriven_5[0], not_7_out);
  not not_7 (not_7_out, undriven_5[1]);
  not not_8 (not_8_out, undriven_5[0]);
  and and_16 (and_16_out, not_8_out, undriven_5[1]);
  and and_17 (and_21_out[2], and_14_out, undriven_6[2]);
  and and_18 (and_21_out[1], and_14_out, undriven_6[1]);
  and and_19 (and_22_out[1], and_14_out, undriven_7[1]);
  and and_20 (and_22_out[2], and_14_out, undriven_7[2]);
  RAM #(.addrWidth(4)) ram_2 (
    .addr(undriven_7), .data(ram_2_data), .sel(1'b1), .clk(not_5_out), .ld(not_6_out), .clr(1'b0));
  assign ram_2_data = and_16_out ? undriven_9 : 8'bz;  // Controlled_Buffer controlled_buffer_3
  and and_21 (and_21_out[0], and_14_out, undriven_6[0]);
  and and_22 (and_22_out[0], and_14_out, undriven_7[0]);
  assign controlled_buffer_4_out = and_15_out ? ram_2_data : 8'bz;  // Controlled_Buffer controlled_buffer_4
  and and_23 (and_31_out[3], and_25_out, undriven_11[3]);
  and and_24 (and_32_out[3], and_25_out, undriven_12[3]);
  and and_25 (and_25_out, undriven_10[0], undriven_10[1]);
  not not_9 (not_9_out, undriven_10[1]);
  not not_10 (not_10_out, undriven_10[0]);
  and and_26 (and_31_out[2], and_25_out, undriven_11[2]);
  and and_27 (and_32_out[2], and_25_out, undriven_12[2]);
  RAM #(.addrWidth(4)) ram_3 (
    .addr(undriven_12), .data(ram_3_data), .sel(1'b1), .clk(not_12_out), .ld(not_11_out), .clr(1'b0));
  not not_11 (not_11_out, and_29_out);
  not not_12 (not_12_out, undriven_13);
  and and_28 (and_28_out, undriven_10[0], not_9_out);
  and and_29 (and_29_out, not_10_out, undriven_10[1]);
  and and_30 (and_31_out[1], and_25_out, undriven_11[1]);
  and and_31 (and_31_out[0], and_25_out, undriven_11[0]);
  and and_32 (and_32_out[0], and_25_out, undriven_12[0]);
  and and_33 (and_32_out[1], and_25_out, undriven_12[1]);
  assign controlled_buffer_5_out = and_28_out ? ram_3_data : 8'bz;  // Controlled_Buffer controlled_buffer_5
  assign ram_3_data = and_29_out ? undriven_14 : 8'bz;  // Controlled_Buffer controlled_buffer_6
endmodule
